# Fritzing sketch Frankenbot-0.2 (saved by Fritzing 0.9.3b)
breadboards: 1

parts:
  Part1 = Adafruit PWM Servo Featherwing [part_number="Adafruit #2928"]
  VCC1 = 4 x AAA Battery Mount
  S1 = Toggle Switch [package=THT]
  U1 = V_REG_LD1117VXX [package=78xxl]
  C1 = Ceramic Capacitor [capacitance=100nF package="100 mil [THT, multilayer]"]
  C2 = Capacitor Polarized [package=nippon_f80]
  R1 = Resistor [tolerance=±5% resistance=220 package="0603 [SMD]"]
  R2 = Resistor [tolerance=±5% resistance=220 package="0603 [SMD]"]
  Q1 = TRANSISTOR_NPN [package=to-92]
  Q2 = TRANSISTOR_NPN [package=to-92]
  D1 = Rectifier Diode [part_number=1N4001 package="300 mil [THT]"]
  D2 = Rectifier Diode [part_number=1N4001 package="300 mil [THT]"]
  M1 = DC Motor
  M2 = DC Motor

nets:
  N1: Part1.PWRIN, S1.L2
  GND: Part1.GND, Part1.I, VCC1.-, U1.GND, C1.0, C2.+, Q1.E, Q2.E
  N2: Part1.PWM_7, R1.Pin_0
  N3: Part1.V+, D1.cathode, D2.cathode, M1.pin_1, M2.pin_2
  N4: Part1.PWM_4, R2.Pin_0
  N5: Part1.SCL, U1.OUT, C2.-
  N6: VCC1.+, S1.COM
  N7: U1.IN, C1.1
  N8: R1.Pin_1, Q1.B
  N9: R2.Pin_1, Q2.B
  N10: Q1.C, D1.anode, M1.pin_2
  N11: Q2.C, D2.anode, M2.pin_1

notes:
  3.3V Power Rail
  6V Power Rail

custom parts:
  Adafruit PWM Servo Featherwing: This is the 8-Channel PWM or Servo​ FeatherWing, you can add 8 x 12-bit PWM outputs to your Feather board. You want to make a cool robot, maybe a hexapod walker, or maybe just a piece of art with a lot of moving parts. Or maybe you want to drive a lot of LEDs with precise PWM output. What now? You could give up OR you could just get our handy PWM and Servo FeatherWing. It's a lot like our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
